// Logisim project ALU.circ as structural Verilog: 1 circuit, main circuit ALU
module ALU (
  input  [31:0] A,
  input  [31:0] B,
  input  [4:0] Shift,
  input  [3:0] Codop,
  input  CarryIn,
  output [31:0] S,
  output [3:0] Flags
);

  wire C_ADC, C_CMN, C_CMP, C_LSL, C_LSR, C_ROR, C_RSB, C_SBS, not_2_out, subtractor_5_bout, V_ADC, V_CMN,
       V_CMP, V_RSB, V_SBS, xnor_1_out, xnor_2_out, xnor_5_out, xnor_6_out, xnor_7_out, xor_2_out, xor_3_out,
       xor_4_out, xor_5_out, xor_6_out;
  wire [4:0] subtractor_1_out, subtractor_2_out, subtractor_3_out;
  wire [30:0] multiplexer_2_out, R_O_R;
  wire [31:0] A_N_D, ADC, ASR, BIC, CMN, CMP, EOR, LSL, LSR, MUL, multiplexer_3_out, MVN, not_1_out, ORR,
       RSB, SBS;
  wire [31:1] shifter_1_out, shifter_2_out;

  Subtractor #(.width(5)) subtractor_1 (.a({5{1'b0}}), .b(Shift), .out(subtractor_1_out));  // open: bin, bout
  assign A_N_D = 32'h7fffffff & 32'h7fffffff;  // AND_Gate and_1, 32 bits wide
  Adder #(.width(32)) adder_1 (.a(32'h7fffffff), .b(32'h7fffffff), .out(CMN), .cout(C_CMN));  // open: cin
  assign EOR = 32'h7fffffff ^ 32'h7fffffff;  // XOR_Gate xor_1, 32 bits wide
  Shifter #(.shift("lr"), .width(32)) shifter_1 (
    .in(32'h7fffffff), .\dist (subtractor_1_out), .out({shifter_1_out, C_LSL}));
  Shifter #(.shift("lr"), .width(32)) shifter_2 (
    .in(32'h7fffffff), .\dist (subtractor_2_out), .out({shifter_2_out, C_LSR}));
  Subtractor #(.width(5)) subtractor_2 (.a(Shift), .b(5'b00001), .out(subtractor_2_out));  // open: bin, bout
  Subtractor #(.width(5)) subtractor_3 (.a(Shift), .b(5'b00001), .out(subtractor_3_out));  // open: bin, bout
  Shifter #(.width(32)) shifter_3 (.in(32'h7fffffff), .\dist (Shift), .out(LSL));
  Shifter #(.shift("lr"), .width(32)) shifter_4 (.in(32'h7fffffff), .\dist (Shift), .out(LSR));
  Shifter #(.shift("ar"), .width(32)) shifter_5 (.in(32'h7fffffff), .\dist (Shift), .out(ASR));
  Shifter #(.width(32)) shifter_6 (.\dist (subtractor_3_out));  // open: in, out
  Subtractor #(.width(32)) subtractor_4 (.a({32{1'b0}}), .b(32'h7fffffff), .out(RSB), .bout(C_RSB));  // open: bin
  assign not_1_out = ~32'h7fffffff;  // NOT_Gate not_1, 32 bits wide
  Adder #(.width(32)) adder_2 (.a(32'h7fffffff), .b(32'h7fffffff), .out(ADC), .cin(CarryIn), .cout(C_ADC));
  not not_2 (not_2_out, CarryIn);
  Subtractor #(.width(32)) subtractor_5 (
    .a(32'h7fffffff), .b(32'h7fffffff), .out(SBS), .bin(not_2_out), .bout(subtractor_5_bout));
  not not_3 (C_SBS, subtractor_5_bout);
  Shifter #(.shift("rr"), .width(32)) shifter_7 (.in(32'h7fffffff), .\dist (Shift), .out({C_ROR, R_O_R}));
  assign BIC = not_1_out & 32'h7fffffff;  // AND_Gate and_2, 32 bits wide
  Multiplexer #(.select(4), .width(32)) multiplexer_1 (
    .in0(A_N_D), .in1(EOR), .in2(LSL), .in3(LSR), .in4(ASR), .in5(ADC), .in6(SBS), .in7({C_ROR, R_O_R}),
    .in8({32{1'b0}}), .in9(RSB), .in10({32{1'b0}}), .in11(CMN), .in12(ORR), .in13(MUL), .in14(BIC),
    .in15(MVN), .out(S), .sel(Codop));
  assign MVN = ~32'h7fffffff;  // NOT_Gate not_4, 32 bits wide
  xnor xnor_1 (xnor_1_out, 1'b0, 1'b0);
  xnor xnor_2 (xnor_2_out, 1'b0, 1'b0);
  assign ORR = 32'h7fffffff | 32'h7fffffff;  // OR_Gate or_1, 32 bits wide
  Subtractor #(.width(32)) subtractor_6 (.a(32'h7fffffff), .b(32'h7fffffff), .out(CMP), .bout(C_CMP));  // open: bin
  Multiplier #(.width(32)) multiplier_1 (.a(32'h7fffffff), .b(32'h7fffffff), .out(MUL));  // open: cin, cout
  xor xor_2 (xor_2_out, 1'b0, 1'b0);
  xor xor_3 (xor_3_out, CMP[31], 1'b0);
  // XNOR_Gate xnor_3 has open pins: in0=xnor_1_out, in1=ADC[31], out=open
  // XNOR_Gate xnor_4 has open pins: in0=xnor_2_out, in1=SBS[31], out=open
  and and_3 (V_CMP, xor_2_out, xor_3_out);
  xnor xnor_5 (xnor_5_out, 1'b0, 1'b0);
  xor xor_4 (xor_4_out, 1'b0, CMN[31]);
  xnor xnor_6 (xnor_6_out, 1'b0, 1'b0);
  xor xor_5 (xor_5_out, 1'b0, ADC[31]);
  xnor xnor_7 (xnor_7_out, 1'b0, 1'b0);
  xor xor_6 (xor_6_out, 1'b0, SBS[31]);
  Multiplexer #(.select(4), .width(32)) multiplexer_2 (
    .in0(A_N_D), .in1(EOR), .in2(LSL), .in3(LSR), .in4(ASR), .in5(ADC), .in6(SBS), .in7({C_ROR, R_O_R}),
    .in8(A_N_D), .in9(RSB), .in10(CMP), .in11(CMN), .in12(ORR), .in13(MUL), .in14(BIC), .in15(MVN),
    .out({Flags[2], multiplexer_2_out}), .sel(Codop));
  Multiplexer #(.select(4), .width(32)) multiplexer_3 (
    .in0(A_N_D), .in1(EOR), .in2(LSL), .in3(LSR), .in4(ASR), .in5(ADC), .in6(SBS), .in7({C_ROR, R_O_R}),
    .in8(A_N_D), .in9(RSB), .in10(CMP), .in11(CMN), .in12(ORR), .in13(MUL), .in14(BIC), .in15(MVN),
    .out(multiplexer_3_out), .sel(Codop));
  xnor xnor_8 (V_RSB, 1'b0, RSB[31]);
  and and_4 (V_CMN, xnor_5_out, xor_4_out);
  and and_5 (V_ADC, xnor_6_out, xor_5_out);
  and and_6 (V_SBS, xnor_7_out, xor_6_out);
  nor nor_1 (Flags[3], multiplexer_3_out[0], multiplexer_3_out[1], multiplexer_3_out[2], multiplexer_3_out[3], multiplexer_3_out[4], multiplexer_3_out[5], multiplexer_3_out[6], multiplexer_3_out[7], multiplexer_3_out[8], multiplexer_3_out[9], multiplexer_3_out[10], multiplexer_3_out[11], multiplexer_3_out[12], multiplexer_3_out[13], multiplexer_3_out[14], multiplexer_3_out[15], multiplexer_3_out[16], multiplexer_3_out[17], multiplexer_3_out[18], multiplexer_3_out[19], multiplexer_3_out[20], multiplexer_3_out[21], multiplexer_3_out[22], multiplexer_3_out[23], multiplexer_3_out[24], multiplexer_3_out[25], multiplexer_3_out[26], multiplexer_3_out[27], multiplexer_3_out[28], multiplexer_3_out[29], multiplexer_3_out[30], multiplexer_3_out[31]);
  Multiplexer #(.select(4)) multiplexer_4 (
    .in0(1'b0), .in1(1'b0), .in2(C_LSL), .in3(C_LSR), .in4(C_LSR), .in5(C_ADC), .in6(C_SBS), .in7(C_ROR),
    .in8(1'b0), .in9(1'b0), .in10(C_CMP), .in11(C_CMN), .in12(1'b0), .in13(1'b0), .in14(1'b0), .in15(1'b0),
    .out(Flags[1]), .sel(Codop));
  Multiplexer #(.select(4)) multiplexer_5 (
    .in0(1'b0), .in1(1'b0), .in2(1'b0), .in3(1'b0), .in4(1'b0), .in5(V_ADC), .in6(V_SBS), .in7(1'b0),
    .in8(1'b0), .in9(V_RSB), .in10(V_CMP), .in11(V_CMN), .in12(1'b0), .in13(1'b0), .in14(1'b0), .in15(1'b0),
    .out(Flags[0]), .sel(Codop));

  // Other names for the same wires on the sheet: N = Flags[2]; V = Flags[0]; C = Flags[1]; Z = Flags[3];
  //   op[3:0] = Codop; R_O_R[31] = C_ROR

  // Notes on the sheet:
  //   Note: for ROR, C = N
  //   Note 2: assume that shift > 0 for LSL and LSR
  //   TST 
  //   TST 
  //   CMP might be fucked
  //   CARRY HERE
endmodule
