// Logisim project BancDeRegistres.circ as structural Verilog: 1 circuit, main circuit BancRegistre
module BancRegistre (
  input  [2:0] RegA,
  input  [2:0] RegB,
  input  [31:0] DataIn,
  input  [2:0] RegDest,
  input  Clk,
  input  Reset,
  output [31:0] AOut,
  output [31:0] BOut,
  output [31:0] R0,
  output [31:0] R1,
  output [31:0] R2,
  output [31:0] R3,
  output [31:0] R4,
  output [31:0] R5,
  output [31:0] R6,
  output [31:0] R7
);

  wire Reset0, Reset1, Reset2, Reset3, Reset4, Reset5, Reset6, Reset7, WE0, WE1, WE2, WE3, WE4, WE5, WE6, WE7;
  wire [31:0] demultiplexer_1_out0, demultiplexer_1_out1, demultiplexer_1_out2, demultiplexer_1_out3,
       demultiplexer_1_out4, demultiplexer_1_out5, demultiplexer_1_out6, demultiplexer_1_out7;

  Multiplexer #(.select(3), .width(32)) multiplexer_1 (
    .in0(R0), .in1(R1), .in2(R2), .in3(R3), .in4(R4), .in5(R5), .in6(R6), .in7(R7), .out(BOut), .sel(RegB));
  Multiplexer #(.select(3), .width(32)) multiplexer_2 (
    .in0(R0), .in1(R1), .in2(R2), .in3(R3), .in4(R4), .in5(R5), .in6(R6), .in7(R7), .out(AOut), .sel(RegA));
  Demultiplexer #(.select(3), .width(32)) demultiplexer_1 (
    .out0(demultiplexer_1_out0), .out1(demultiplexer_1_out1), .out2(demultiplexer_1_out2),
    .out3(demultiplexer_1_out3), .out4(demultiplexer_1_out4), .out5(demultiplexer_1_out5),
    .out6(demultiplexer_1_out6), .out7(demultiplexer_1_out7), .in(DataIn), .sel(RegDest));
  Register #(.width(32)) register_1 (.D(demultiplexer_1_out4), .en(WE4), .clk(Clk), .Q(R4), .clr(Reset4));
  Register #(.width(32)) register_2 (.D(demultiplexer_1_out5), .en(WE5), .clk(Clk), .Q(R5), .clr(Reset5));
  Register #(.width(32)) register_3 (.D(demultiplexer_1_out6), .en(WE6), .clk(Clk), .Q(R6), .clr(Reset6));
  Register #(.width(32)) register_4 (.D(demultiplexer_1_out7), .en(WE7), .clk(Clk), .Q(R7), .clr(Reset7));
  Register #(.width(32)) register_5 (.D(demultiplexer_1_out0), .en(WE0), .clk(Clk), .Q(R0), .clr(Reset0));
  Register #(.width(32)) register_6 (.D(demultiplexer_1_out1), .en(WE1), .clk(Clk), .Q(R1), .clr(Reset1));
  Register #(.width(32)) register_7 (.D(demultiplexer_1_out2), .en(WE2), .clk(Clk), .Q(R2), .clr(Reset2));
  Register #(.width(32)) register_8 (.D(demultiplexer_1_out3), .en(WE3), .clk(Clk), .Q(R3), .clr(Reset3));
  Demultiplexer #(.select(3)) demultiplexer_2 (
    .out0(WE0), .out1(WE1), .out2(WE2), .out3(WE3), .out4(WE4), .out5(WE5), .out6(WE6), .out7(WE7),
    .in(1'b1), .sel(RegDest));
  Demultiplexer #(.select(3)) demultiplexer_3 (
    .out0(Reset0), .out1(Reset1), .out2(Reset2), .out3(Reset3), .out4(Reset4), .out5(Reset5), .out6(Reset6),
    .out7(Reset7), .in(Reset), .sel(RegDest));

  // Other names for the same wires on the sheet: MyClock = Clk

  // Notes on the sheet:
  //   Lecture d'un registre donnée dans AOut
  //   Lecture d'un registre donnée dans BOut
  //   Ecrite DataIn dans le registre choisi
  //   Activation du WE du registre choisi
  //   Reset du registre choisi
endmodule
