// Logisim project Ctl_Conditional.circ as structural Verilog: 1 circuit, main circuit Conditional
module Conditional (
  input  Enable,
  input  [15:0] Instruction,
  input  Z,
  input  C,
  input  N,
  input  V,
  output [10:0] Offset,
  output Verified
);

  wire and_1_out, and_2_out, multiplexer_1_out, not_1_out, not_2_out, not_3_out, not_4_out, or_1_out,
       or_2_out, verified_t, xnor_1_out, xnor_2_out, xor_1_out, xor_2_out;
  wire [10:0] bit_extender_1_out;

  and and_1 (and_1_out, ~Z, C);  // AND_Gate
  or or_1 (or_1_out, ~C, Z);  // OR_Gate
  xnor xnor_1 (xnor_1_out, N, V);
  xor xor_1 (xor_1_out, N, V);
  not not_1 (not_1_out, Z);
  not not_2 (not_2_out, C);
  not not_3 (not_3_out, N);
  not not_4 (not_4_out, V);
  or or_2 (or_2_out, Z, xor_2_out);
  xor xor_2 (xor_2_out, N, V);
  and and_2 (and_2_out, ~Z, xnor_2_out);  // AND_Gate
  xnor xnor_2 (xnor_2_out, N, V);
  and and_3 (Verified, Enable, verified_t);
  Multiplexer #(.select(4)) multiplexer_1 (
    .in0(Z), .in1(not_1_out), .in2(C), .in3(not_2_out), .in4(N), .in5(not_3_out), .in6(V), .in7(not_4_out),
    .in8(and_1_out), .in9(or_1_out), .in10(xnor_1_out), .in11(xor_1_out), .in12(and_2_out), .in13(or_2_out),
    .in14(1'b1), .in15(1'b0), .out(multiplexer_1_out), .sel(Instruction[11:8]));
  Multiplexer multiplexer_2 (.in0(1'b0), .in1(multiplexer_1_out), .out(verified_t), .sel(Instruction[12]));
  assign bit_extender_1_out = {{3{Instruction[7]}}, Instruction[7:0]};  // Bit_Extender bit_extender_1
  Multiplexer #(.width(11)) multiplexer_3 (
    .in0(Instruction[10:0]), .in1(bit_extender_1_out), .out(Offset), .sel(Instruction[12]));

  // Other names for the same wires on the sheet: imm8[7:0] = Instruction[7:0]; imm11[10:0] = Instruction[10:0];
  //   rest[11:0] = Instruction[11:0]; cond[3:0] = Instruction[11:8]; b12 = Instruction[12]
endmodule
