// Logisim project Ctl_Data_Processing.circ as structural Verilog: 1 circuit, main circuit Data_Processing
module Data_Processing (
  input  Enable,
  input  [15:0] Instruction,
  output [2:0] Rd,
  output [2:0] Rn,
  output [2:0] Rm,
  output [3:0] ALU_Opcode,
  output [3:0] Flags_Update_Mask
);

  wire and_2_out, and_3_out, and_4_out, and_5_out, and_6_out, and_7_out, C, not_1_out, rnRES;
  wire [0:0] Flags;
  wire [2:0] rm_t, rn_t;

  and and_1 (rnRES, Instruction[9], ~Instruction[7], Instruction[6]);  // AND_Gate
  Multiplexer #(.width(3)) multiplexer_1 (.in0(Instruction[2:0]), .in1(Instruction[5:3]), .out(rn_t), .sel(rnRES));
  Multiplexer #(.width(3)) multiplexer_2 (.in0(Instruction[2:0]), .in1(Instruction[5:3]), .out(rm_t), .sel(not_1_out));
  not not_1 (not_1_out, rnRES);
  Multiplexer #(.width(3)) multiplexer_3 (.in0(3'b000), .in1(Instruction[2:0]), .out(Rd), .sel(Enable));
  Multiplexer #(.width(3)) multiplexer_4 (.in0(3'b000), .in1(rn_t), .out(Rn), .sel(Enable));
  Multiplexer #(.width(3)) multiplexer_5 (.in0(3'b000), .in1(rm_t), .out(Rm), .sel(Enable));
  Multiplexer #(.width(4)) multiplexer_6 (.in0(4'b0000), .in1(Instruction[9:6]), .out(ALU_Opcode), .sel(Enable));
  Multiplexer #(.width(4)) multiplexer_7 (
    .in0(4'b0000), .in1({2'b11, C, Flags[0]}), .out(Flags_Update_Mask), .sel(Enable));
  and and_2 (and_2_out, rnRES, Instruction[8]);
  not not_2 (C, and_2_out);
  and and_3 (and_3_out, ~Instruction[9], Instruction[8], ~Instruction[7], Instruction[6]);  // AND_Gate
  and and_4 (and_4_out, ~Instruction[9], Instruction[8], Instruction[7], ~Instruction[6]);  // AND_Gate
  and and_5 (and_5_out, Instruction[9], ~Instruction[8], ~Instruction[7], Instruction[6]);  // AND_Gate
  and and_6 (and_6_out, Instruction[9], ~Instruction[8], Instruction[7], ~Instruction[6]);  // AND_Gate
  and and_7 (and_7_out, Instruction[9], ~Instruction[8], Instruction[7], Instruction[6]);  // AND_Gate
  ExactlyOne xor_1 (
    .out(Flags[0]), .in0(and_3_out), .in1(and_4_out), .in2(and_5_out), .in3(and_6_out), .in4(and_7_out));

  // Other names for the same wires on the sheet: V = Flags[0]; Flags[1] = C; bit10 = Instruction[10];
  //   bit11 = Instruction[11]; bit12 = Instruction[12]; bit13 = Instruction[13]; bit14 = Instruction[14];
  //   bit15 = Instruction[15]; bit6 = Instruction[6]; Opcode[3:0] = Instruction[9:6]; bit7 = Instruction[7];
  //   bit8 = Instruction[8]; bit9 = Instruction[9]; bit0 = Instruction[0]; rd_t[2:0] = Instruction[2:0];
  //   rmAP[2:0] = Instruction[2:0]; rnAP[2:0] = Instruction[2:0]; bit1 = Instruction[1]; bit2 = Instruction[2];
  //   bit3 = Instruction[3]; rmAVANT[2:0] = Instruction[5:3]; rnAVANT[2:0] = Instruction[5:3]; bit4 = Instruction[4];
  //   bit5 = Instruction[5]

  // Notes on the sheet:
  //   Note 2: RSB instruction has Rn as 1st operand.
  //   MUL instruction has Rn as 1st operand and Rdm as 2nd operand
  //   For simplification purposes, Rm is used for 1st operand both here and in the ALU.
  //   Note: instructions that does not save the result will still have the second operand as the destination register, the ALU will copy the second register to the destination register
  //   Pull output low on Enable = 0
endmodule
