// Logisim project Ctl_Flags_APSR.circ as structural Verilog: 1 circuit, main circuit Flags_APSR
module Flags_APSR (
  input  [3:0] Update_Mask,
  input  [3:0] Flags_In,
  input  Clk,
  input  Rst,
  output [3:0] Flags_Out
);

  wire [3:0] Res, Sortie1, Sortie2;

  Register #(.width(4)) register_1 (.D(Res), .en(1'b1), .clk(Clk), .Q(Flags_Out), .clr(Rst));
  assign Sortie1 = Update_Mask & Flags_In;  // AND_Gate and_1, 4 bits wide
  assign Sortie2 = ~Update_Mask & Flags_Out;  // AND_Gate and_2, 4 bits wide
  assign Res = Sortie1 | Sortie2;  // OR_Gate or_1, 4 bits wide

  // Other names for the same wires on the sheet: Clock = Clk; Current[3:0] = Flags_Out; flagsIn[3:0] = Flags_In;
  //   mask[3:0] = Update_Mask
endmodule
