// Logisim project Ctl_Opcode_Decoder.circ as structural Verilog: 1 circuit, main circuit Opcode_Decoder
module Opcode_Decoder (
  input  [5:0] Opcode,
  output Shift,
  output Data_Processing,
  output Load_Store,
  output SP_Address,
  output Conditional
);

  wire and_2_out, and_3_out;

  and and_1 (Shift, ~Opcode[5], ~Opcode[4]);  // AND_Gate
  and and_2 (and_2_out, Opcode[5], Opcode[4], ~Opcode[3], Opcode[2]);  // AND_Gate
  and and_3 (and_3_out, Opcode[5], Opcode[4], Opcode[3], ~Opcode[2]);  // AND_Gate
  or or_1 (Conditional, and_2_out, and_3_out);
  and and_4 (Data_Processing, ~Opcode[5], Opcode[4], ~Opcode[3], ~Opcode[2], ~Opcode[1], ~Opcode[0]);  // AND_Gate
  and and_5 (Load_Store, Opcode[5], ~Opcode[4], ~Opcode[3], Opcode[2]);  // AND_Gate
  and and_6 (SP_Address, Opcode[5], ~Opcode[4], Opcode[3], Opcode[2]);  // AND_Gate
  and and_7 (SP_Address, Opcode[5], ~Opcode[4], Opcode[3], Opcode[2]);  // AND_Gate

  // Other names for the same wires on the sheet: Data = Data_Processing; Load = Load_Store; bit1 = Opcode[0];
  //   bit2 = Opcode[1]; bit3 = Opcode[2]; bit4 = Opcode[3]; bit5 = Opcode[4]; bit6 = Opcode[5]; SPAdrr = SP_Address

  // Notes on the sheet:
  //   Shift, add, sub, mov
  //   Load/Store
  //   SP Address
  //   Conditional branch
  //   Data Processing
endmodule
