// Logisim project Ctl_SP_Address.circ as structural Verilog: 1 circuit, main circuit SP_Address
module SP_Address (
  input  [31:0] Stack_Pointer,
  input  [15:0] Instruction,
  input  Enable,
  output [31:0] New_Stack_Pointer,
  output Write_Enable
);

  wire [31:0] bit0A6Extended, bit0A6Final, NewStackPointer, res1, res2;

  assign bit0A6Extended = {{25{Instruction[6]}}, Instruction[6:0]};  // Bit_Extender bit_extender_1
  Multiplier #(.width(32)) multiplier_1 (.a(bit0A6Extended), .b(32'h4), .out(bit0A6Final));  // open: cin, cout
  Adder #(.width(32)) adder_1 (.a(bit0A6Final), .b(Stack_Pointer), .out(res1));  // open: cin, cout
  Subtractor #(.width(32)) subtractor_1 (.a(Stack_Pointer), .b(bit0A6Final), .out(res2));  // open: bin, bout
  Multiplexer #(.width(32)) multiplexer_1 (.in0(res1), .in1(res2), .out(NewStackPointer), .sel(Instruction[7]));
  Multiplexer #(.width(32)) multiplexer_2 (
    .in0({32{1'b0}}), .in1(NewStackPointer), .out(New_Stack_Pointer), .sel(Enable));

  assign Write_Enable = Enable;

  // Other names for the same wires on the sheet: bit0A6[6:0] = Instruction[6:0]; bit7 = Instruction[7];
  //   StackPointer[31:0] = Stack_Pointer

  // Notes on the sheet:
  //   Pull output low on Enable = 0
endmodule
