// Logisim project Ctl_Shift_Add_Sub_Mov.circ as structural Verilog: 1 circuit, main circuit Shift_Add_Sub_Mov
module Shift_Add_Sub_Mov (
  input  Enable,
  input  [15:0] Instruction,
  output Carry,
  output Imm32_Enable,
  output [2:0] Rm,
  output [3:0] Flags_Update_Mask,
  output [2:0] Rn,
  output [4:0] Imm5,
  output [2:0] Rd,
  output [31:0] Imm32,
  output [3:0] ALU_Opcode
);

  wire and_1_out, and_2_out, and_3_out, and_4_out, and_5_out, and_6_out, and_7_out, and_8_out, C, carry_t,
       imm32_enable_t, nand_1_out, or_2_out;
  wire [0:0] flags;
  wire [2:0] rd_t, rn_t;
  wire [3:0] ALU_opcode_t, multiplexer_16_out, multiplexer_17_out, multiplexer_18_out;
  wire [4:0] imm5_t;
  wire [31:0] bit_extender_1_out, bit_extender_2_out, bit_extender_3_out, imm32_t, immOut,
       multiplexer_13_out, negator_1_out;

  Multiplexer #(.width(4)) multiplexer_1 (
    .in0(4'b0000), .in1({2'b11, C, flags[0]}), .out(Flags_Update_Mask), .sel(Enable));
  Multiplexer #(.width(5)) multiplexer_2 (.in0({5{1'b0}}), .in1(imm5_t), .out(Imm5), .sel(Enable));
  Multiplexer multiplexer_3 (.in0(1'b0), .in1(carry_t), .out(Carry), .sel(Enable));
  Multiplexer multiplexer_4 (.in0(1'b0), .in1(imm32_enable_t), .out(Imm32_Enable), .sel(Enable));
  Multiplexer #(.width(3)) multiplexer_5 (.in0(3'b000), .in1(Instruction[8:6]), .out(Rm), .sel(Enable));
  Multiplexer #(.width(3)) multiplexer_6 (.in0(3'b000), .in1(rd_t), .out(Rd), .sel(Enable));
  Multiplexer #(.width(32)) multiplexer_7 (.in0({32{1'b0}}), .in1(imm32_t), .out(Imm32), .sel(Enable));
  Multiplexer #(.width(3)) multiplexer_8 (.in0(3'b000), .in1(rn_t), .out(Rn), .sel(Enable));
  Multiplexer #(.width(4)) multiplexer_9 (.in0(4'b0000), .in1(ALU_opcode_t), .out(ALU_Opcode), .sel(Enable));
  Multiplexer #(.width(3)) multiplexer_10 (
    .in0(Instruction[2:0]), .in1(Instruction[10:8]), .out(rd_t), .sel(Instruction[13]));
  and and_1 (and_1_out, ~Instruction[13], nand_1_out);  // AND_Gate
  nand nand_1 (nand_1_out, Instruction[12], Instruction[11]);
  and and_2 (and_2_out, ~Instruction[13], ~Instruction[12], ~Instruction[11], Instruction[10]);  // AND_Gate
  Multiplexer #(.width(5)) multiplexer_11 (.in0({5{1'b0}}), .in1(Instruction[10:6]), .out(imm5_t), .sel(and_1_out));
  Multiplexer #(.width(3)) multiplexer_12 (
    .in0(Instruction[5:3]), .in1(Instruction[10:8]), .out(rn_t), .sel(and_3_out));
  and and_3 (and_3_out, Instruction[13], Instruction[12]);
  assign bit_extender_1_out = {{29{1'b0}}, Instruction[8:6]};  // Bit_Extender bit_extender_1
  Comparator #(.width(4)) comparator_1 (.a(ALU_opcode_t), .b(4'b0110), .eq(carry_t));  // open: gt, lt
  Multiplexer #(.width(32)) multiplexer_13 (
    .in0({32{1'b0}}), .in1(bit_extender_1_out), .out(multiplexer_13_out), .sel(and_2_out));
  or or_1 (imm32_enable_t, and_2_out, Instruction[13]);
  assign bit_extender_2_out = {{24{1'b0}}, Instruction[7:0]};  // Bit_Extender bit_extender_2
  and and_4 (and_4_out, Instruction[13], ~Instruction[12], ~Instruction[11]);  // AND_Gate
  assign bit_extender_3_out = {{24{1'b0}}, Instruction[7:0]};  // Bit_Extender bit_extender_3
  Negator #(.width(32)) negator_1 (.in(bit_extender_2_out), .out(negator_1_out));
  Multiplexer #(.width(32)) multiplexer_14 (
    .in0(bit_extender_3_out), .in1(negator_1_out), .out(immOut), .sel(and_4_out));
  Multiplexer #(.width(32)) multiplexer_15 (
    .in0(multiplexer_13_out), .in1(immOut), .out(imm32_t), .sel(Instruction[13]));
  and and_5 (and_5_out, Instruction[13], ~Instruction[12], ~Instruction[11]);  // AND_Gate
  not not_1 (C, and_5_out);
  Multiplexer #(.width(4)) multiplexer_16 (
    .in0(4'b0101), .in1(4'b0110), .out(multiplexer_16_out), .sel(Instruction[9]));
  Multiplexer #(.select(2), .width(4)) multiplexer_17 (
    .in0(4'b0010), .in1(4'b0011), .in2(4'b0100), .in3(multiplexer_16_out), .out(multiplexer_17_out),
    .sel(Instruction[12:11]));
  Multiplexer #(.select(2), .width(4)) multiplexer_18 (
    .in0(4'b1001), .in1(4'b1010), .in2(4'b0101), .in3(4'b0110), .out(multiplexer_18_out),
    .sel(Instruction[12:11]));
  and and_6 (and_6_out, ~Instruction[13], ~Instruction[12], ~Instruction[11]);  // AND_Gate
  and and_7 (and_7_out, ~Instruction[13], ~Instruction[12], Instruction[11]);  // AND_Gate
  and and_8 (and_8_out, Instruction[13], ~Instruction[12], ~Instruction[11]);  // AND_Gate
  Multiplexer #(.width(4)) multiplexer_19 (
    .in0(multiplexer_17_out), .in1(multiplexer_18_out), .out(ALU_opcode_t), .sel(Instruction[13]));
  or or_2 (or_2_out, and_6_out, and_7_out, and_8_out);
  not not_2 (flags[0], or_2_out);

  // Other names for the same wires on the sheet: b11 = Instruction[11]; b12 = Instruction[12]; V = flags[0];
  //   flags[1] = C; b6 = Instruction[6]; imm3[2:0] = Instruction[8:6]; imm5Intermediare[4:0] = Instruction[10:6];
  //   imm8[7:0] = Instruction[7:0]; rm_t[2:0] = Instruction[8:6]; b7 = Instruction[7]; b8 = Instruction[8];
  //   rd_middle[2:0] = Instruction[10:8]; rn_first[2:0] = Instruction[10:8]; b9 = Instruction[9];
  //   b10 = Instruction[10]; b_last = Instruction[0]; rd_last[2:0] = Instruction[2:0]; b1 = Instruction[1];
  //   b2 = Instruction[2]; b3 = Instruction[3]; rn_middle[2:0] = Instruction[5:3]; b4 = Instruction[4];
  //   b5 = Instruction[5]; b13 = Instruction[13]

  // Notes on the sheet:
  //   Note: ALU uses Rn register for shifts. Use Rn instead of Rm for shifts (immediate) here too
  //   Note 3: Imm32_Enable forces the use of the immediate for Rm register
  //   Note 2: MOV uses RSB ALU opcode with Imm8 reversed so that it is copied to output register
  //   Pull output low on Enable = 0
  //   MUX for every output
  //   only ADD and SUB use Rm
  //   Enable carry for SUB since it is reversed in ALU
  //   ALU will use Imm32 instead of Rm
endmodule
